# Fritzing sketch Noah v2 (saved by Fritzing 0.8.7b)
breadboards: 1

parts:
  Netduino1 = Netduino Plus 2
  RHT1 = Humidity and Temperature Sensor RHT03
  S1 = Toggle Switch [package=THT]

nets:
  N1: Netduino1.D10, S1.COM
  N2: Netduino1.D5, Netduino1.D4, RHT1.Data-signal
  +5V: Netduino1.+5V, RHT1.Vcc, S1.L1
  N3: Netduino1.GND, RHT1.GND_2, S1.L2

notes:
  Flood Sensor
  RHT03 - Temperature & Humidity

custom parts:
  Netduino Plus 2: An open-source electronics platform using the .NET Micro Framework
